// Logisim project P3.circ as structural Verilog: 9 circuits, main circuit main
module main (
  input  RST,
  output [31:0] Instr,
  output [31:0] pc,
  output RegWrite,
  output [4:0] RegAddr,
  output [31:0] RegData,
  output MemWrite,
  output [31:0] MemAddr,
  output [31:0] MemData
);

  wire ALU_Cmp, ALUSrc_B, ALUSrc_S, CLK;
  wire [1:0] ExtOp, MemOp, RegDst, RegSrc;
  wire [2:0] nPC_sel;
  wire [3:0] ALUOp;
  wire [4:0] multiplexer_5_out;
  wire [31:0] adder_1_out, ALU_Res, grf_1_rd1, grf_1_rd2, Imm32, Mem, multiplexer_1_out, multiplexer_4_out;

  Clock clock_1 (.out(CLK));
  Multiplexer #(.width(32)) multiplexer_1 (
    .in0({pc[31:28], Instr[25:0], 2'b00}), .in1(grf_1_rd1), .out(multiplexer_1_out), .sel(nPC_sel[2]));  // open: en
  IFU ifu_1 (
    .CLK(CLK), .RST(RST), .True(ALU_Cmp), .Branch(nPC_sel), .Imm32(Imm32), .Inst(Instr), .out_8(pc),
    .in_6(multiplexer_1_out));
  assign MemAddr = ALU_Res & 32'hfffffffc;  // AND_Gate and_1, 32 bits wide
  Adder #(.width(32)) adder_1 (.a(pc), .b(32'h4), .out(adder_1_out));  // open: cin, cout
  Multiplexer #(.select(2), .width(32)) multiplexer_2 (
    .in0(ALU_Res), .in1(Mem), .in2(adder_1_out), .out(RegData), .sel(RegSrc));  // open: in3, en
  Multiplexer #(.select(2), .width(5)) multiplexer_3 (
    .in0(Instr[15:11]), .in1(Instr[20:16]), .in2({5{1'b1}}), .out(RegAddr), .sel(RegDst));  // open: in3, en
  GRF grf_1 (
    .rst(RST), .clk(CLK), .WD(RegData), .RD1(grf_1_rd1), .A1(Instr[25:21]), .RD2(grf_1_rd2),
    .A2(Instr[20:16]), .A3(RegAddr), .WE(RegWrite));
  Controller controller_1 (
    .OP(Instr[31:26]), .FUNC(Instr[5:0]), .RegDst(RegDst), .ALUSrc({ALUSrc_B, ALUSrc_S}), .RegSrc(RegSrc),
    .RegWrite(RegWrite), .nPC_sel(nPC_sel), .ExtOp(ExtOp), .ALUOp(ALUOp), .MemOp({MemWrite, MemOp}));
  DM dm_1 (
    .MemOp({MemWrite, MemOp}), .RawWD(grf_1_rd2), .Addr(ALU_Res[13:0]), .CLK(CLK), .RST(RST), .WD(MemData),
    .RD(Mem));
  Multiplexer #(.width(32)) multiplexer_4 (
    .in0(grf_1_rd2), .in1(Imm32), .out(multiplexer_4_out), .sel(ALUSrc_B));  // open: en
  Multiplexer #(.width(5)) multiplexer_5 (
    .in0(grf_1_rd1[4:0]), .in1(Instr[10:6]), .out(multiplexer_5_out), .sel(ALUSrc_S));  // open: en
  ALU alu_1 (
    .A(grf_1_rd1), .B(multiplexer_4_out), .ALUOp(ALUOp), .Out(ALU_Res), .CMP(ALU_Cmp),
    .in_4(multiplexer_5_out));
  Ext ext_1 (.Imm(Instr[15:0]), .Type(ExtOp), .out_3(Imm32));

  // Other names for the same wires on the sheet: FUNC[5:0] = Instr[5:0]; Imm16[15:0] = Instr[15:0];
  //   Inst[31:0] = Instr; instr_idx[25:0] = Instr[25:0]; OP[5:0] = Instr[31:26]; MemOp[2] = MemWrite;
  //   MemWD[31:0] = MemData; RegWA[4:0] = RegAddr; RegWD[31:0] = RegData; RegWrt = RegWrite
endmodule

module GRF (
  input  rst,
  input  clk,
  input  [31:0] WD,
  input  [4:0] A1,
  input  [4:0] A2,
  input  [4:0] A3,
  input  WE,
  output [31:0] RD1,
  output [31:0] RD2
);

  wire A1x0, A1x1, A1x2, A1x3, A1x4, A1x5, A1x6, A1x7, A1y0, A1y1, A1y2, A1y3, A2x0, A2x1, A2x2, A2x3, A2x4,
       A2x5, A2x6, A2x7, A2y0, A2y1, A2y2, A2y3, A3x0, A3x1, A3x2, A3x3, A3x4, A3x5, A3x6, A3x7, A3y0, A3y1,
       A3y2, A3y3, and_2_out, and_3_out, and_4_out, and_5_out, and_6_out, and_7_out, and_8_out, and_9_out,
       and_10_out, and_11_out, and_12_out, and_13_out, and_14_out, and_15_out, and_16_out, and_17_out,
       and_18_out, and_19_out, and_20_out, and_21_out, and_22_out, and_23_out, and_24_out, and_25_out,
       and_26_out, and_27_out, and_28_out, and_29_out, and_30_out, and_31_out, and_32_out, and_33_out,
       and_34_out, and_35_out, and_36_out, and_37_out, and_38_out, and_39_out, and_40_out, and_41_out,
       and_42_out, and_43_out, and_44_out, and_45_out, and_46_out, and_47_out, and_48_out, and_49_out,
       and_50_out, and_51_out, and_52_out, and_53_out, and_54_out, and_55_out, and_56_out, and_57_out,
       and_58_out, and_59_out, and_60_out, and_61_out, and_62_out, and_63_out, and_64_out, and_65_out,
       and_66_out, and_67_out, and_68_out, and_69_out, and_70_out, and_71_out, and_72_out, and_73_out,
       and_74_out, and_75_out, and_76_out, and_77_out, and_78_out, and_79_out, and_80_out, and_81_out,
       and_82_out, and_83_out, and_84_out, and_85_out, and_86_out, and_87_out, and_88_out, and_89_out,
       and_90_out, and_91_out, and_92_out, and_93_out, and_94_out, and_95_out, and_96_out, and_97_out;
  wire [4:0] and_1_out, bit_extender_1_out;
  wire [31:0] register_1_q, register_2_q, register_3_q, register_4_q, register_5_q, register_6_q,
       register_7_q, register_8_q, register_9_q, register_10_q, register_11_q, register_12_q, register_13_q,
       register_14_q, register_15_q, register_16_q, register_17_q, register_18_q, register_19_q,
       register_20_q, register_21_q, register_22_q, register_23_q, register_24_q, register_25_q,
       register_26_q, register_27_q, register_28_q, register_29_q, register_30_q, register_31_q,
       register_32_q;

  assign and_1_out = A3 & bit_extender_1_out;  // AND_Gate and_1, 5 bits wide
  assign bit_extender_1_out = {{4{WE}}, WE};  // Bit_Extender bit_extender_1
  Decoder #(.select(3), .enable("false")) decoder_1 (
    .out0(A1x0), .out1(A1x1), .out2(A1x2), .out3(A1x3), .out4(A1x4), .out5(A1x5), .out6(A1x6), .out7(A1x7),
    .sel(A1[2:0]));
  Decoder #(.select(3), .enable("false")) decoder_2 (
    .out0(A2x0), .out1(A2x1), .out2(A2x2), .out3(A2x3), .out4(A2x4), .out5(A2x5), .out6(A2x6), .out7(A2x7),
    .sel(A2[2:0]));
  Decoder #(.select(3), .enable("false")) decoder_3 (
    .out0(A3x0), .out1(A3x1), .out2(A3x2), .out3(A3x3), .out4(A3x4), .out5(A3x5), .out6(A3x6), .out7(A3x7),
    .sel(and_1_out[2:0]));
  Decoder #(.select(2), .enable("false")) decoder_4 (.out0(A1y0), .out1(A1y1), .out2(A1y2), .out3(A1y3), .sel(A1[4:3]));
  Decoder #(.select(2), .enable("false")) decoder_5 (.out0(A2y0), .out1(A2y1), .out2(A2y2), .out3(A2y3), .sel(A2[4:3]));
  Decoder #(.select(2), .enable("false")) decoder_6 (
    .out0(A3y0), .out1(A3y1), .out2(A3y2), .out3(A3y3), .sel(and_1_out[4:3]));
  and and_2 (and_2_out, A3y0, A3x0);
  and and_3 (and_3_out, A3y1, A3x0);
  and and_4 (and_4_out, A3y2, A3x0);
  and and_5 (and_5_out, A3y3, A3x0);
  Register #(.width(32)) register_1 (.D({32{1'b0}}), .en(and_2_out), .Q(register_1_q), .clk(clk), .clr(rst));
  Register #(.width(32)) register_2 (.D(WD), .en(and_3_out), .Q(register_2_q), .clk(clk), .clr(rst));
  Register #(.width(32)) register_3 (.D(WD), .en(and_4_out), .Q(register_3_q), .clk(clk), .clr(rst));
  Register #(.width(32)) register_4 (.D(WD), .en(and_5_out), .Q(register_4_q), .clk(clk), .clr(rst));
  and and_6 (and_6_out, A1x0, A1y0);
  assign RD1 = and_6_out ? register_1_q : 32'bz;  // Controlled_Buffer controlled_buffer_1
  assign RD2 = and_7_out ? register_1_q : 32'bz;  // Controlled_Buffer controlled_buffer_2
  and and_7 (and_7_out, A2x0, A2y0);
  and and_8 (and_8_out, A1x0, A1y1);
  assign RD1 = and_8_out ? register_2_q : 32'bz;  // Controlled_Buffer controlled_buffer_3
  assign RD2 = and_9_out ? register_2_q : 32'bz;  // Controlled_Buffer controlled_buffer_4
  and and_9 (and_9_out, A2x0, A2y1);
  and and_10 (and_10_out, A1x0, A1y2);
  assign RD1 = and_10_out ? register_3_q : 32'bz;  // Controlled_Buffer controlled_buffer_5
  assign RD2 = and_11_out ? register_3_q : 32'bz;  // Controlled_Buffer controlled_buffer_6
  and and_11 (and_11_out, A2x0, A2y2);
  and and_12 (and_12_out, A1x0, A1y3);
  assign RD1 = and_12_out ? register_4_q : 32'bz;  // Controlled_Buffer controlled_buffer_7
  assign RD2 = and_13_out ? register_4_q : 32'bz;  // Controlled_Buffer controlled_buffer_8
  and and_13 (and_13_out, A2x0, A2y3);
  and and_14 (and_14_out, A3y0, A3x1);
  and and_15 (and_15_out, A3y1, A3x1);
  and and_16 (and_16_out, A3y2, A3x1);
  and and_17 (and_17_out, A3y3, A3x1);
  Register #(.width(32)) register_5 (.D(WD), .en(and_14_out), .Q(register_5_q), .clk(clk), .clr(rst));
  Register #(.width(32)) register_6 (.D(WD), .en(and_15_out), .Q(register_6_q), .clk(clk), .clr(rst));
  Register #(.width(32)) register_7 (.D(WD), .en(and_16_out), .Q(register_7_q), .clk(clk), .clr(rst));
  Register #(.width(32)) register_8 (.D(WD), .en(and_17_out), .Q(register_8_q), .clk(clk), .clr(rst));
  and and_18 (and_18_out, A1x1, A1y0);
  assign RD1 = and_18_out ? register_5_q : 32'bz;  // Controlled_Buffer controlled_buffer_9
  assign RD2 = and_19_out ? register_5_q : 32'bz;  // Controlled_Buffer controlled_buffer_10
  and and_19 (and_19_out, A2x1, A2y0);
  and and_20 (and_20_out, A1x1, A1y1);
  assign RD1 = and_20_out ? register_6_q : 32'bz;  // Controlled_Buffer controlled_buffer_11
  assign RD2 = and_21_out ? register_6_q : 32'bz;  // Controlled_Buffer controlled_buffer_12
  and and_21 (and_21_out, A2x1, A2y1);
  and and_22 (and_22_out, A1x1, A1y2);
  assign RD1 = and_22_out ? register_7_q : 32'bz;  // Controlled_Buffer controlled_buffer_13
  assign RD2 = and_23_out ? register_7_q : 32'bz;  // Controlled_Buffer controlled_buffer_14
  and and_23 (and_23_out, A2x1, A2y2);
  and and_24 (and_24_out, A1x1, A1y3);
  assign RD1 = and_24_out ? register_8_q : 32'bz;  // Controlled_Buffer controlled_buffer_15
  assign RD2 = and_25_out ? register_8_q : 32'bz;  // Controlled_Buffer controlled_buffer_16
  and and_25 (and_25_out, A2x1, A2y3);
  and and_26 (and_26_out, A3y0, A3x2);
  and and_27 (and_27_out, A3y1, A3x2);
  and and_28 (and_28_out, A3y2, A3x2);
  and and_29 (and_29_out, A3y3, A3x2);
  Register #(.width(32)) register_9 (.D(WD), .en(and_26_out), .Q(register_9_q), .clk(clk), .clr(rst));
  Register #(.width(32)) register_10 (.D(WD), .en(and_27_out), .Q(register_10_q), .clk(clk), .clr(rst));
  Register #(.width(32)) register_11 (.D(WD), .en(and_28_out), .Q(register_11_q), .clk(clk), .clr(rst));
  Register #(.width(32)) register_12 (.D(WD), .en(and_29_out), .Q(register_12_q), .clk(clk), .clr(rst));
  and and_30 (and_30_out, A1x2, A1y0);
  assign RD1 = and_30_out ? register_9_q : 32'bz;  // Controlled_Buffer controlled_buffer_17
  assign RD2 = and_31_out ? register_9_q : 32'bz;  // Controlled_Buffer controlled_buffer_18
  and and_31 (and_31_out, A2x2, A2y0);
  and and_32 (and_32_out, A1x2, A1y1);
  assign RD1 = and_32_out ? register_10_q : 32'bz;  // Controlled_Buffer controlled_buffer_19
  assign RD2 = and_33_out ? register_10_q : 32'bz;  // Controlled_Buffer controlled_buffer_20
  and and_33 (and_33_out, A2x2, A2y1);
  and and_34 (and_34_out, A1x2, A1y2);
  assign RD1 = and_34_out ? register_11_q : 32'bz;  // Controlled_Buffer controlled_buffer_21
  assign RD2 = and_35_out ? register_11_q : 32'bz;  // Controlled_Buffer controlled_buffer_22
  and and_35 (and_35_out, A2x2, A2y2);
  and and_36 (and_36_out, A1x2, A1y3);
  assign RD1 = and_36_out ? register_12_q : 32'bz;  // Controlled_Buffer controlled_buffer_23
  assign RD2 = and_37_out ? register_12_q : 32'bz;  // Controlled_Buffer controlled_buffer_24
  and and_37 (and_37_out, A2x2, A2y3);
  and and_38 (and_38_out, A3y0, A3x3);
  and and_39 (and_39_out, A3y1, A3x3);
  and and_40 (and_40_out, A3y2, A3x3);
  and and_41 (and_41_out, A3y3, A3x3);
  Register #(.width(32)) register_13 (.D(WD), .en(and_38_out), .Q(register_13_q), .clk(clk), .clr(rst));
  Register #(.width(32)) register_14 (.D(WD), .en(and_39_out), .Q(register_14_q), .clk(clk), .clr(rst));
  Register #(.width(32)) register_15 (.D(WD), .en(and_40_out), .Q(register_15_q), .clk(clk), .clr(rst));
  Register #(.width(32)) register_16 (.D(WD), .en(and_41_out), .Q(register_16_q), .clk(clk), .clr(rst));
  and and_42 (and_42_out, A1x3, A1y0);
  assign RD1 = and_42_out ? register_13_q : 32'bz;  // Controlled_Buffer controlled_buffer_25
  assign RD2 = and_43_out ? register_13_q : 32'bz;  // Controlled_Buffer controlled_buffer_26
  and and_43 (and_43_out, A2x3, A2y0);
  and and_44 (and_44_out, A1x3, A1y1);
  assign RD1 = and_44_out ? register_14_q : 32'bz;  // Controlled_Buffer controlled_buffer_27
  assign RD2 = and_45_out ? register_14_q : 32'bz;  // Controlled_Buffer controlled_buffer_28
  and and_45 (and_45_out, A2x3, A2y1);
  and and_46 (and_46_out, A1x3, A1y2);
  assign RD1 = and_46_out ? register_15_q : 32'bz;  // Controlled_Buffer controlled_buffer_29
  assign RD2 = and_47_out ? register_15_q : 32'bz;  // Controlled_Buffer controlled_buffer_30
  and and_47 (and_47_out, A2x3, A2y2);
  and and_48 (and_48_out, A1x3, A1y3);
  assign RD1 = and_48_out ? register_16_q : 32'bz;  // Controlled_Buffer controlled_buffer_31
  assign RD2 = and_49_out ? register_16_q : 32'bz;  // Controlled_Buffer controlled_buffer_32
  and and_49 (and_49_out, A2x3, A2y3);
  Register #(.width(32)) register_17 (.D(WD), .en(and_50_out), .Q(register_17_q), .clk(clk), .clr(rst));
  and and_50 (and_50_out, A3y0, A3x4);
  Register #(.width(32)) register_18 (.D(WD), .en(and_51_out), .Q(register_18_q), .clk(clk), .clr(rst));
  and and_51 (and_51_out, A3y1, A3x4);
  Register #(.width(32)) register_19 (.D(WD), .en(and_52_out), .Q(register_19_q), .clk(clk), .clr(rst));
  and and_52 (and_52_out, A3y2, A3x4);
  Register #(.width(32)) register_20 (.D(WD), .en(and_53_out), .Q(register_20_q), .clk(clk), .clr(rst));
  and and_53 (and_53_out, A3y3, A3x4);
  and and_54 (and_54_out, A1x4, A1y0);
  assign RD1 = and_54_out ? register_17_q : 32'bz;  // Controlled_Buffer controlled_buffer_33
  assign RD2 = and_55_out ? register_17_q : 32'bz;  // Controlled_Buffer controlled_buffer_34
  and and_55 (and_55_out, A2x4, A2y0);
  and and_56 (and_56_out, A1x4, A1y1);
  assign RD1 = and_56_out ? register_18_q : 32'bz;  // Controlled_Buffer controlled_buffer_35
  assign RD2 = and_57_out ? register_18_q : 32'bz;  // Controlled_Buffer controlled_buffer_36
  and and_57 (and_57_out, A2x4, A2y1);
  and and_58 (and_58_out, A1x4, A1y2);
  assign RD1 = and_58_out ? register_19_q : 32'bz;  // Controlled_Buffer controlled_buffer_37
  assign RD2 = and_59_out ? register_19_q : 32'bz;  // Controlled_Buffer controlled_buffer_38
  and and_59 (and_59_out, A2x4, A2y2);
  and and_60 (and_60_out, A1x4, A1y3);
  assign RD1 = and_60_out ? register_20_q : 32'bz;  // Controlled_Buffer controlled_buffer_39
  assign RD2 = and_61_out ? register_20_q : 32'bz;  // Controlled_Buffer controlled_buffer_40
  and and_61 (and_61_out, A2x4, A2y3);
  Register #(.width(32)) register_21 (.D(WD), .en(and_62_out), .Q(register_21_q), .clk(clk), .clr(rst));
  and and_62 (and_62_out, A3y0, A3x5);
  Register #(.width(32)) register_22 (.D(WD), .en(and_63_out), .Q(register_22_q), .clk(clk), .clr(rst));
  and and_63 (and_63_out, A3y1, A3x5);
  Register #(.width(32)) register_23 (.D(WD), .en(and_64_out), .Q(register_23_q), .clk(clk), .clr(rst));
  and and_64 (and_64_out, A3y2, A3x5);
  Register #(.width(32)) register_24 (.D(WD), .en(and_65_out), .Q(register_24_q), .clk(clk), .clr(rst));
  and and_65 (and_65_out, A3y3, A3x5);
  and and_66 (and_66_out, A1x5, A1y0);
  assign RD1 = and_66_out ? register_21_q : 32'bz;  // Controlled_Buffer controlled_buffer_41
  assign RD2 = and_67_out ? register_21_q : 32'bz;  // Controlled_Buffer controlled_buffer_42
  and and_67 (and_67_out, A2x5, A2y0);
  and and_68 (and_68_out, A1x5, A1y1);
  assign RD1 = and_68_out ? register_22_q : 32'bz;  // Controlled_Buffer controlled_buffer_43
  assign RD2 = and_69_out ? register_22_q : 32'bz;  // Controlled_Buffer controlled_buffer_44
  and and_69 (and_69_out, A2x5, A2y1);
  and and_70 (and_70_out, A1x5, A1y2);
  assign RD1 = and_70_out ? register_23_q : 32'bz;  // Controlled_Buffer controlled_buffer_45
  assign RD2 = and_71_out ? register_23_q : 32'bz;  // Controlled_Buffer controlled_buffer_46
  and and_71 (and_71_out, A2x5, A2y2);
  and and_72 (and_72_out, A1x5, A1y3);
  assign RD1 = and_72_out ? register_24_q : 32'bz;  // Controlled_Buffer controlled_buffer_47
  assign RD2 = and_73_out ? register_24_q : 32'bz;  // Controlled_Buffer controlled_buffer_48
  and and_73 (and_73_out, A2x5, A2y3);
  Register #(.width(32)) register_25 (.D(WD), .en(and_74_out), .Q(register_25_q), .clk(clk), .clr(rst));
  and and_74 (and_74_out, A3y0, A3x6);
  Register #(.width(32)) register_26 (.D(WD), .en(and_75_out), .Q(register_26_q), .clk(clk), .clr(rst));
  and and_75 (and_75_out, A3y1, A3x6);
  Register #(.width(32)) register_27 (.D(WD), .en(and_76_out), .Q(register_27_q), .clk(clk), .clr(rst));
  and and_76 (and_76_out, A3y2, A3x6);
  Register #(.width(32)) register_28 (.D(WD), .en(and_77_out), .Q(register_28_q), .clk(clk), .clr(rst));
  and and_77 (and_77_out, A3y3, A3x6);
  and and_78 (and_78_out, A1x6, A1y0);
  and and_79 (and_79_out, A2x6, A2y0);
  and and_80 (and_80_out, A1x6, A1y1);
  and and_81 (and_81_out, A2x6, A2y1);
  and and_82 (and_82_out, A1x6, A1y2);
  and and_83 (and_83_out, A2x6, A2y2);
  and and_84 (and_84_out, A1x6, A1y3);
  and and_85 (and_85_out, A2x6, A2y3);
  assign RD1 = and_78_out ? register_25_q : 32'bz;  // Controlled_Buffer controlled_buffer_49
  assign RD2 = and_79_out ? register_25_q : 32'bz;  // Controlled_Buffer controlled_buffer_50
  assign RD1 = and_80_out ? register_26_q : 32'bz;  // Controlled_Buffer controlled_buffer_51
  assign RD2 = and_81_out ? register_26_q : 32'bz;  // Controlled_Buffer controlled_buffer_52
  assign RD1 = and_82_out ? register_27_q : 32'bz;  // Controlled_Buffer controlled_buffer_53
  assign RD2 = and_83_out ? register_27_q : 32'bz;  // Controlled_Buffer controlled_buffer_54
  assign RD1 = and_84_out ? register_28_q : 32'bz;  // Controlled_Buffer controlled_buffer_55
  assign RD2 = and_85_out ? register_28_q : 32'bz;  // Controlled_Buffer controlled_buffer_56
  Register #(.width(32)) register_29 (.D(WD), .en(and_86_out), .Q(register_29_q), .clk(clk), .clr(rst));
  and and_86 (and_86_out, A3y0, A3x7);
  Register #(.width(32)) register_30 (.D(WD), .en(and_87_out), .Q(register_30_q), .clk(clk), .clr(rst));
  and and_87 (and_87_out, A3y1, A3x7);
  Register #(.width(32)) register_31 (.D(WD), .en(and_88_out), .Q(register_31_q), .clk(clk), .clr(rst));
  and and_88 (and_88_out, A3y2, A3x7);
  Register #(.width(32)) register_32 (.D(WD), .en(and_89_out), .Q(register_32_q), .clk(clk), .clr(rst));
  and and_89 (and_89_out, A3y3, A3x7);
  and and_90 (and_90_out, A1x7, A1y0);
  and and_91 (and_91_out, A2x7, A2y0);
  and and_92 (and_92_out, A1x7, A1y1);
  and and_93 (and_93_out, A2x7, A2y1);
  and and_94 (and_94_out, A1x7, A1y2);
  and and_95 (and_95_out, A2x7, A2y2);
  and and_96 (and_96_out, A1x7, A1y3);
  and and_97 (and_97_out, A2x7, A2y3);
  assign RD1 = and_90_out ? register_29_q : 32'bz;  // Controlled_Buffer controlled_buffer_57
  assign RD2 = and_91_out ? register_29_q : 32'bz;  // Controlled_Buffer controlled_buffer_58
  assign RD1 = and_92_out ? register_30_q : 32'bz;  // Controlled_Buffer controlled_buffer_59
  assign RD2 = and_93_out ? register_30_q : 32'bz;  // Controlled_Buffer controlled_buffer_60
  assign RD1 = and_94_out ? register_31_q : 32'bz;  // Controlled_Buffer controlled_buffer_61
  assign RD2 = and_95_out ? register_31_q : 32'bz;  // Controlled_Buffer controlled_buffer_62
  assign RD1 = and_96_out ? register_32_q : 32'bz;  // Controlled_Buffer controlled_buffer_63
  assign RD2 = and_97_out ? register_32_q : 32'bz;  // Controlled_Buffer controlled_buffer_64
endmodule

module IFU (
  input  CLK,
  input  RST,
  input  True,
  input  [2:0] Branch,
  input  [31:0] Imm32,
  input  [31:0] in_6,
  output [31:0] Inst,
  output [31:0] out_8
);

  wire and_1_out, Jump;
  wire [11:0] Addr;
  wire [31:0] adder_1_out, adder_2_out, multiplexer_1_out, NPC, shifter_1_out;

  or or_1 (Jump, Branch[1], Branch[2]);
  Adder #(.width(32)) adder_1 (.a(out_8), .b(32'h4), .out(adder_1_out));  // open: cin, cout
  Shifter #(.width(32)) shifter_1 (.in(Imm32), .\dist (5'b00010), .out(shifter_1_out));
  Adder #(.width(32)) adder_2 (.a(adder_1_out), .b(shifter_1_out), .out(adder_2_out));  // open: cin, cout
  and and_1 (and_1_out, True, Branch[0]);
  Multiplexer #(.width(32)) multiplexer_1 (
    .in0(adder_1_out), .in1(adder_2_out), .out(multiplexer_1_out), .sel(and_1_out));  // open: en
  Multiplexer #(.width(32)) multiplexer_2 (.in0(multiplexer_1_out), .in1(in_6), .out(NPC), .sel(Jump));  // open: en
  // Probe on Addr
  PC pc_1 (.NPC(NPC), .CLK(CLK), .PC(out_8), .Addr(Addr), .RST(RST));
  IM im_1 (.Addr(Addr), .out_2(Inst));
  // Probe on Inst

  // Other names for the same wires on the sheet: Branch_t = Branch[0]; Jaddr[31:0] = in_6; PC[31:0] = out_8
endmodule

module IM (
  input  [11:0] Addr,
  output [31:0] out_2
);

  ROM #(.addrWidth(12), .dataWidth(32)) rom_1 (.addr(Addr), .data(out_2));  // open: sel

  // Notes on the sheet:
  //   contents of rom_1 (hex, n*v repeats v):
  //   341c0000 341d0000 34013456 210820 8c010004 ac010004 3c027878 411822 3c051234 34040005 0 ac85ffff
  //   8c83ffff 10650001 1000000d 34670404 10e3000b 0 3c087777 3508ffff 80022 34001100 e65020 34080000
  //   34090001 340a0001 10a4020 1109fffe 1000ffff
endmodule

module PC (
  input  [31:0] NPC,
  input  CLK,
  input  RST,
  output [31:0] PC,
  output [11:0] Addr
);

  wire [31:0] register_1_q, subtractor_1_out;
  wire [31:12] shifter_1_out;

  Subtractor #(.width(32)) subtractor_1 (.a(NPC), .b(32'h3000), .out(subtractor_1_out));  // open: bin, bout
  Register #(.width(32)) register_1 (.D(subtractor_1_out), .Q(register_1_q), .clk(CLK), .clr(RST));  // open: en
  Adder #(.width(32)) adder_1 (.a(32'h3000), .b(register_1_q), .out(PC));  // open: cin, cout
  Shifter #(.width(32), .shift("lr")) shifter_1 (.in(register_1_q), .\dist (5'b00010), .out({shifter_1_out, Addr}));
endmodule

module ALU (
  input  [31:0] A,
  input  [31:0] B,
  input  [3:0] ALUOp,
  input  [4:0] in_4,
  output [31:0] Out,
  output CMP
);

  wire and_2_out, and_3_out, and_4_out, and_5_out, and_6_out, and_7_out, comparator_1_eq, comparator_1_gt,
       comparator_1_lt, decoder_1_out10, decoder_1_out11, decoder_1_out12, decoder_1_out13, decoder_1_out14,
       decoder_1_out15, not_1_out, not_2_out, not_3_out;
  wire [31:0] ADD, AND, OR, SLL, SLT, SRL, SUB;

  assign AND = A & B;  // AND_Gate and_1, 32 bits wide
  assign OR = A | B;  // OR_Gate or_1, 32 bits wide
  Adder #(.width(32)) adder_1 (.a(A), .b(B), .out(ADD));  // open: cin, cout
  Subtractor #(.width(32)) subtractor_1 (.a(A), .b(B), .out(SUB));  // open: bin, bout
  Shifter #(.width(32)) shifter_1 (.in(B), .\dist (in_4), .out(SLL));
  Shifter #(.width(32), .shift("lr")) shifter_2 (.in(B), .\dist (in_4), .out(SRL));
  Comparator #(.width(32)) comparator_1 (
    .a(A), .b(B), .gt(comparator_1_gt), .eq(comparator_1_eq), .lt(comparator_1_lt));
  Decoder #(.select(4)) decoder_1 (
    .out10(decoder_1_out10), .out11(decoder_1_out11), .out12(decoder_1_out12), .out13(decoder_1_out13),
    .out14(decoder_1_out14), .out15(decoder_1_out15), .sel(ALUOp));  // open: out0, out1, out2, out3, out4, out5, out6, out7, out8, out9, en
  Multiplexer #(.select(4), .width(32)) multiplexer_1 (
    .in0(ADD), .in1(SUB), .in2(AND), .in3(OR), .in4(SLL), .in5(SLT), .in6(SRL), .in10({32{1'b0}}),
    .in11({32{1'b0}}), .in12({32{1'b0}}), .in13({32{1'b0}}), .in14({32{1'b0}}), .in15({32{1'b0}}), .out(Out),
    .sel(ALUOp));  // open: in7, in8, in9, en
  assign SLT = {{31{1'b0}}, comparator_1_lt};  // Bit_Extender bit_extender_1
  not not_1 (not_1_out, comparator_1_eq);
  not not_2 (not_2_out, comparator_1_gt);
  not not_3 (not_3_out, comparator_1_lt);
  and and_2 (and_2_out, not_1_out, decoder_1_out10);
  and and_3 (and_3_out, comparator_1_lt, decoder_1_out11);
  and and_4 (and_4_out, not_2_out, decoder_1_out12);
  and and_5 (and_5_out, comparator_1_gt, decoder_1_out13);
  and and_6 (and_6_out, not_3_out, decoder_1_out14);
  and and_7 (and_7_out, comparator_1_eq, decoder_1_out15);
  or or_2 (CMP, and_2_out, and_3_out, and_4_out, and_5_out, and_6_out, and_7_out);

  // Other names for the same wires on the sheet: Shift[4:0] = in_4

  // Notes on the sheet:
  //   0000:ADD
  //   0001:SUB
  //   0010:AND
  //   0011:OR
  //   0100:SLL
  //   0110:SRL
  //   0101:SLT
  //   1010:NE
  //   1011:LT
  //   1100:LE
  //   1101:GT
  //   1110:GE
  //   1111:EQ
endmodule

module Ext (
  input  [15:0] Imm,
  input  [1:0] Type,
  output [31:0] out_3
);

  wire [31:0] bit_extender_1_out, bit_extender_2_out, shifter_1_out;

  assign bit_extender_1_out = {{16{1'b0}}, Imm};  // Bit_Extender bit_extender_1
  assign bit_extender_2_out = {{16{Imm[15]}}, Imm};  // Bit_Extender bit_extender_2
  Shifter #(.width(32)) shifter_1 (.in(bit_extender_1_out), .\dist (5'b10000), .out(shifter_1_out));
  Multiplexer #(.select(2), .width(32)) multiplexer_1 (
    .in0(bit_extender_1_out), .in1(bit_extender_2_out), .in2(shifter_1_out), .out(out_3), .sel(Type));  // open: in3, en

  // Notes on the sheet:
  //   00:Zero
  //   01:Sign
  //   10:High-half
endmodule

module Controller (
  input  [5:0] OP,
  input  [5:0] FUNC,
  output [1:0] RegDst,
  output [1:0] RegSrc,
  output RegWrite,
  output [1:0] ExtOp,
  output [3:0] ALUOp,
  output [1:0] ALUSrc,
  output [2:0] nPC_sel,
  output [2:0] MemOp
);

  wire _0Ext, ADDIU, ADDU, ALU_ADD, ALU_AND, ALU_EQ, ALU_OR, ALU_SLL, ALU_SLT, ALU_SRL, ALU_SUB, AND,
       and_1_out, and_7_out, ANDI, Bytewise, Halfwordwise, HighExt, J, JALR, JR, LB, LH, LW, NOP, not_1_out,
       not_2_out, not_3_out, not_4_out, not_5_out, not_6_out, not_7_out, not_8_out, not_9_out, not_10_out,
       not_11_out, not_12_out, not_13_out, not_14_out, not_15_out, not_16_out, not_17_out, not_18_out,
       not_19_out, not_20_out, not_21_out, not_22_out, not_23_out, not_24_out, not_25_out, not_26_out,
       not_27_out, not_28_out, not_29_out, not_30_out, not_31_out, not_32_out, not_33_out, not_34_out,
       not_35_out, not_36_out, not_37_out, not_38_out, not_39_out, not_40_out, not_41_out, not_42_out,
       not_43_out, not_44_out, not_45_out, not_46_out, not_47_out, not_48_out, not_49_out, not_50_out,
       not_51_out, not_52_out, not_53_out, not_54_out, not_55_out, not_56_out, not_57_out, not_58_out,
       not_59_out, not_60_out, not_61_out, not_62_out, not_63_out, not_64_out, not_65_out, not_66_out,
       not_67_out, not_68_out, not_69_out, not_70_out, not_71_out, not_72_out, not_73_out, not_74_out,
       not_75_out, not_76_out, not_77_out, not_78_out, not_79_out, not_80_out, not_81_out, not_82_out,
       not_83_out, not_84_out, not_85_out, not_86_out, not_87_out, not_88_out, not_89_out, not_90_out,
       not_91_out, not_92_out, not_93_out, not_94_out, not_95_out, not_96_out, not_97_out, not_98_out,
       not_99_out, not_100_out, not_101_out, not_102_out, not_103_out, not_104_out, not_105_out, not_106_out,
       not_107_out, not_108_out, not_109_out, not_110_out, not_111_out, not_112_out, not_113_out,
       not_114_out, not_115_out, not_116_out, not_117_out, not_118_out, not_119_out, not_120_out,
       not_121_out, not_122_out, not_123_out, not_124_out, not_125_out, not_126_out, not_127_out,
       not_128_out, not_129_out, not_130_out, not_131_out, not_132_out, not_133_out, not_134_out,
       not_135_out, not_136_out, not_137_out, not_138_out, not_139_out, not_140_out, not_141_out,
       not_142_out, not_143_out, not_144_out, not_145_out, not_146_out, not_147_out, not_148_out,
       not_149_out, not_150_out, not_151_out, not_152_out, not_153_out, not_154_out, not_155_out,
       not_156_out, not_157_out, not_158_out, not_159_out, not_160_out, not_161_out, not_162_out,
       not_163_out, not_164_out, not_165_out, not_166_out, not_167_out, not_168_out, not_169_out,
       not_170_out, not_171_out, not_172_out, not_173_out, not_174_out, not_175_out, not_176_out,
       not_177_out, not_178_out, not_179_out, not_180_out, not_181_out, not_182_out, not_183_out,
       not_184_out, not_185_out, not_186_out, OR, or_17_out, ORI, SB, SH, SignExt, SLL, SLLV, SLT, SLTI, SRL,
       SW, undriven, undriven_2, undriven_3, undriven_4, undriven_5, undriven_6, undriven_7, undriven_8,
       undriven_9, undriven_10, undriven_11, undriven_12, undriven_13, undriven_14, undriven_15, undriven_16,
       undriven_17, undriven_18, undriven_19, Wordwise;

  not not_1 (not_1_out, undriven);
  not not_2 (not_2_out, undriven_2);
  not not_3 (not_3_out, undriven_3);
  not not_4 (not_4_out, undriven_4);
  not not_5 (not_5_out, undriven_5);
  not not_6 (not_6_out, undriven_6);
  not not_7 (not_7_out, undriven_7);
  not not_8 (not_8_out, undriven_8);
  not not_9 (not_9_out, undriven_9);
  not not_10 (not_10_out, undriven_10);
  not not_11 (not_11_out, undriven_11);
  not not_12 (not_12_out, undriven_12);
  not not_13 (not_13_out, OP[5]);
  not not_14 (not_14_out, OP[4]);
  not not_15 (not_15_out, OP[3]);
  not not_16 (not_16_out, OP[2]);
  not not_17 (not_17_out, OP[1]);
  not not_18 (not_18_out, OP[0]);
  not not_19 (not_19_out, FUNC[5]);
  not not_20 (not_20_out, FUNC[4]);
  not not_21 (not_21_out, FUNC[3]);
  not not_22 (not_22_out, FUNC[2]);
  not not_23 (not_23_out, FUNC[1]);
  not not_24 (not_24_out, FUNC[0]);
  not not_25 (not_25_out, OP[5]);
  not not_26 (not_26_out, OP[4]);
  not not_27 (not_27_out, OP[3]);
  not not_28 (not_28_out, OP[2]);
  not not_29 (not_29_out, OP[1]);
  not not_30 (not_30_out, OP[0]);
  not not_31 (not_31_out, FUNC[4]);
  not not_32 (not_32_out, FUNC[3]);
  not not_33 (not_33_out, FUNC[2]);
  not not_34 (not_34_out, FUNC[1]);
  not not_35 (not_35_out, FUNC[0]);
  not not_36 (not_36_out, OP[5]);
  not not_37 (not_37_out, OP[4]);
  not not_38 (not_38_out, OP[3]);
  not not_39 (not_39_out, OP[2]);
  not not_40 (not_40_out, OP[1]);
  not not_41 (not_41_out, OP[0]);
  not not_42 (not_42_out, FUNC[4]);
  not not_43 (not_43_out, FUNC[3]);
  not not_44 (not_44_out, FUNC[2]);
  not not_45 (not_45_out, FUNC[0]);
  not not_46 (not_46_out, OP[5]);
  not not_47 (not_47_out, OP[4]);
  not not_48 (not_48_out, OP[3]);
  not not_49 (not_49_out, OP[2]);
  not not_50 (not_50_out, OP[1]);
  not not_51 (not_51_out, OP[0]);
  not not_52 (not_52_out, FUNC[4]);
  not not_53 (not_53_out, FUNC[3]);
  not not_54 (not_54_out, FUNC[1]);
  not not_55 (not_55_out, FUNC[0]);
  not not_56 (not_56_out, OP[5]);
  not not_57 (not_57_out, OP[4]);
  not not_58 (not_58_out, OP[3]);
  not not_59 (not_59_out, OP[2]);
  not not_60 (not_60_out, OP[1]);
  not not_61 (not_61_out, OP[0]);
  not not_62 (not_62_out, FUNC[4]);
  not not_63 (not_63_out, FUNC[3]);
  not not_64 (not_64_out, FUNC[1]);
  and and_1 (and_1_out, not_1_out, not_2_out, not_3_out, not_4_out, not_5_out, not_6_out, not_7_out, not_8_out, not_9_out, not_10_out, not_11_out, not_12_out);
  and and_2 (NOP, not_13_out, not_14_out, not_15_out, not_16_out, not_17_out, not_18_out, not_19_out, not_20_out, not_21_out, not_22_out, not_23_out, not_24_out);
  and and_3 (ADDU, not_25_out, not_26_out, not_27_out, not_28_out, not_29_out, not_30_out, FUNC[5], not_31_out, not_32_out, not_33_out, not_34_out, not_35_out);
  and and_4 (ALU_SUB, not_36_out, not_37_out, not_38_out, not_39_out, not_40_out, not_41_out, FUNC[5], not_42_out, not_43_out, not_44_out, FUNC[1], not_45_out);
  and and_5 (AND, not_46_out, not_47_out, not_48_out, not_49_out, not_50_out, not_51_out, FUNC[5], not_52_out, not_53_out, FUNC[2], not_54_out, not_55_out);
  and and_6 (OR, not_56_out, not_57_out, not_58_out, not_59_out, not_60_out, not_61_out, FUNC[5], not_62_out, not_63_out, FUNC[2], not_64_out, FUNC[0]);
  not not_65 (not_65_out, undriven_13);
  not not_66 (not_66_out, undriven_14);
  not not_67 (not_67_out, undriven_15);
  not not_68 (not_68_out, undriven_16);
  not not_69 (not_69_out, undriven_17);
  not not_70 (not_70_out, undriven_18);
  not not_71 (not_71_out, OP[5]);
  not not_72 (not_72_out, OP[4]);
  not not_73 (not_73_out, OP[1]);
  not not_74 (not_74_out, OP[0]);
  not not_75 (not_75_out, OP[5]);
  not not_76 (not_76_out, OP[4]);
  not not_77 (not_77_out, OP[1]);
  not not_78 (not_78_out, OP[4]);
  not not_79 (not_79_out, OP[3]);
  not not_80 (not_80_out, OP[2]);
  not not_81 (not_81_out, OP[4]);
  not not_82 (not_82_out, OP[2]);
  not not_83 (not_83_out, OP[5]);
  not not_84 (not_84_out, OP[4]);
  not not_85 (not_85_out, OP[3]);
  not not_86 (not_86_out, OP[1]);
  not not_87 (not_87_out, OP[0]);
  not not_88 (not_88_out, OP[5]);
  not not_89 (not_89_out, OP[4]);
  not not_90 (not_90_out, OP[5]);
  not not_91 (not_91_out, OP[4]);
  not not_92 (not_92_out, OP[2]);
  not not_93 (not_93_out, OP[1]);
  not not_94 (not_94_out, OP[5]);
  not not_95 (not_95_out, OP[4]);
  not not_96 (not_96_out, OP[2]);
  not not_97 (not_97_out, OP[0]);
  and and_7 (and_7_out, not_65_out, not_66_out, not_67_out, not_68_out, not_69_out, not_70_out);
  and and_8 (ANDI, not_71_out, not_72_out, OP[3], OP[2], not_73_out, not_74_out);
  and and_9 (ORI, not_75_out, not_76_out, OP[3], OP[2], not_77_out, OP[0]);
  and and_10 (LW, OP[5], not_78_out, not_79_out, not_80_out, OP[1], OP[0]);
  and and_11 (SW, OP[5], not_81_out, OP[3], not_82_out, OP[1], OP[0]);
  and and_12 (ALU_EQ, not_83_out, not_84_out, not_85_out, OP[2], not_86_out, not_87_out);
  and and_13 (HighExt, not_88_out, not_89_out, OP[3], OP[2], OP[1], OP[0]);
  and and_14 (ADDIU, not_90_out, not_91_out, OP[3], not_92_out, not_93_out, OP[0]);
  and and_15 (SLTI, not_94_out, not_95_out, OP[3], not_96_out, OP[1], not_97_out);
  not not_98 (not_98_out, OP[5]);
  not not_99 (not_99_out, OP[4]);
  not not_100 (not_100_out, OP[3]);
  not not_101 (not_101_out, OP[2]);
  not not_102 (not_102_out, OP[1]);
  not not_103 (not_103_out, OP[0]);
  not not_104 (not_104_out, FUNC[5]);
  not not_105 (not_105_out, FUNC[4]);
  not not_106 (not_106_out, FUNC[3]);
  not not_107 (not_107_out, FUNC[2]);
  not not_108 (not_108_out, FUNC[1]);
  not not_109 (not_109_out, FUNC[0]);
  not not_110 (not_110_out, OP[5]);
  not not_111 (not_111_out, OP[4]);
  not not_112 (not_112_out, OP[3]);
  not not_113 (not_113_out, OP[2]);
  not not_114 (not_114_out, OP[1]);
  not not_115 (not_115_out, OP[0]);
  not not_116 (not_116_out, FUNC[5]);
  not not_117 (not_117_out, FUNC[4]);
  not not_118 (not_118_out, FUNC[3]);
  not not_119 (not_119_out, FUNC[1]);
  not not_120 (not_120_out, FUNC[0]);
  not not_121 (not_121_out, OP[5]);
  not not_122 (not_122_out, OP[4]);
  not not_123 (not_123_out, OP[3]);
  not not_124 (not_124_out, OP[2]);
  not not_125 (not_125_out, OP[1]);
  not not_126 (not_126_out, OP[0]);
  not not_127 (not_127_out, FUNC[4]);
  not not_128 (not_128_out, FUNC[2]);
  not not_129 (not_129_out, FUNC[0]);
  not not_130 (not_130_out, OP[5]);
  not not_131 (not_131_out, OP[4]);
  not not_132 (not_132_out, OP[3]);
  not not_133 (not_133_out, OP[2]);
  not not_134 (not_134_out, OP[1]);
  not not_135 (not_135_out, OP[0]);
  not not_136 (not_136_out, FUNC[5]);
  not not_137 (not_137_out, FUNC[4]);
  not not_138 (not_138_out, FUNC[2]);
  not not_139 (not_139_out, FUNC[1]);
  not not_140 (not_140_out, OP[5]);
  not not_141 (not_141_out, OP[4]);
  not not_142 (not_142_out, OP[3]);
  not not_143 (not_143_out, OP[2]);
  not not_144 (not_144_out, OP[1]);
  not not_145 (not_145_out, OP[0]);
  not not_146 (not_146_out, FUNC[5]);
  not not_147 (not_147_out, FUNC[4]);
  not not_148 (not_148_out, FUNC[2]);
  not not_149 (not_149_out, FUNC[1]);
  not not_150 (not_150_out, FUNC[0]);
  and and_16 (SLL, not_98_out, not_99_out, not_100_out, not_101_out, not_102_out, not_103_out, not_104_out, not_105_out, not_106_out, not_107_out, not_108_out, not_109_out);
  and and_17 (SLLV, not_110_out, not_111_out, not_112_out, not_113_out, not_114_out, not_115_out, not_116_out, not_117_out, not_118_out, FUNC[2], not_119_out, not_120_out);
  and and_18 (SLT, not_121_out, not_122_out, not_123_out, not_124_out, not_125_out, not_126_out, FUNC[5], not_127_out, FUNC[3], not_128_out, FUNC[1], not_129_out);
  and and_19 (JALR, not_130_out, not_131_out, not_132_out, not_133_out, not_134_out, not_135_out, not_136_out, not_137_out, FUNC[3], not_138_out, not_139_out, FUNC[0]);
  and and_20 (JR, not_140_out, not_141_out, not_142_out, not_143_out, not_144_out, not_145_out, not_146_out, not_147_out, FUNC[3], not_148_out, not_149_out, not_150_out);
  not not_151 (not_151_out, OP[5]);
  not not_152 (not_152_out, OP[4]);
  not not_153 (not_153_out, OP[3]);
  not not_154 (not_154_out, OP[2]);
  not not_155 (not_155_out, OP[0]);
  not not_156 (not_156_out, OP[5]);
  not not_157 (not_157_out, OP[4]);
  not not_158 (not_158_out, OP[3]);
  not not_159 (not_159_out, OP[2]);
  not not_160 (not_160_out, OP[4]);
  not not_161 (not_161_out, OP[2]);
  not not_162 (not_162_out, OP[1]);
  not not_163 (not_163_out, OP[4]);
  not not_164 (not_164_out, OP[2]);
  not not_165 (not_165_out, OP[1]);
  not not_166 (not_166_out, OP[0]);
  not not_167 (not_167_out, OP[4]);
  not not_168 (not_168_out, OP[3]);
  not not_169 (not_169_out, OP[2]);
  not not_170 (not_170_out, OP[1]);
  not not_171 (not_171_out, OP[4]);
  not not_172 (not_172_out, OP[3]);
  not not_173 (not_173_out, OP[2]);
  not not_174 (not_174_out, OP[1]);
  not not_175 (not_175_out, OP[0]);
  and and_21 (J, not_151_out, not_152_out, not_153_out, not_154_out, OP[1], not_155_out);
  and and_22 (RegDst[1], not_156_out, not_157_out, not_158_out, not_159_out, OP[1], OP[0]);
  and and_23 (SH, OP[5], not_160_out, OP[3], not_161_out, not_162_out, OP[0]);
  and and_24 (SB, OP[5], not_163_out, OP[3], not_164_out, not_165_out, not_166_out);
  and and_25 (LH, OP[5], not_167_out, not_168_out, not_169_out, not_170_out, OP[0]);
  and and_26 (LB, OP[5], not_171_out, not_172_out, not_173_out, not_174_out, not_175_out);
  or or_1 (ALUSrc[0], SLL, SRL);
  or or_2 (RegSrc[0], LW, LH, LB);
  or or_3 (ALUSrc[1], ANDI, ORI, ADDIU, HighExt, SLTI, SW, LW, SH, SB, LH, LB);
  not not_176 (not_176_out, OP[5]);
  not not_177 (not_177_out, OP[4]);
  not not_178 (not_178_out, OP[3]);
  not not_179 (not_179_out, OP[2]);
  not not_180 (not_180_out, OP[1]);
  not not_181 (not_181_out, OP[0]);
  not not_182 (not_182_out, FUNC[5]);
  not not_183 (not_183_out, FUNC[4]);
  not not_184 (not_184_out, FUNC[3]);
  not not_185 (not_185_out, FUNC[2]);
  not not_186 (not_186_out, FUNC[0]);
  and and_27 (SRL, not_176_out, not_177_out, not_178_out, not_179_out, not_180_out, not_181_out, not_182_out, not_183_out, not_184_out, not_185_out, FUNC[1], not_186_out);
  or or_4 (MemOp[2], SW, SH, SB);
  buf or_5 (nPC_sel[0], ALU_EQ);  // OR_Gate
  or or_6 (nPC_sel[1], J, RegDst[1]);
  or or_7 (nPC_sel[2], JR, JALR);
  or or_8 (RegWrite, ADDU, ALU_SUB, AND, OR, SLLV, SLT, ANDI, ORI, ADDIU, HighExt, SLL, SLTI, LW, RegDst[1], LH, LB, JALR, SRL);
  Priority_Encoder #(.select(2)) priority_encoder_1 (
    .in0(_0Ext), .in1(SignExt), .in2(HighExt), .in3(undriven_19), .out(ExtOp));  // open: gs, en_out, en_in
  Priority_Encoder #(.select(4)) priority_encoder_2 (
    .in0(ALU_ADD), .in1(ALU_SUB), .in2(ALU_AND), .in3(ALU_OR), .in4(ALU_SLL), .in5(ALU_SLT), .in6(ALU_SRL),
    .in15(ALU_EQ), .out(ALUOp));  // open: in7, in8, in9, in10, in11, in12, in13, in14, gs, en_out, en_in
  or or_9 (ALU_ADD, ADDU, ADDIU, HighExt, SW, LW, ALU_EQ, SH, SB, LH, LB);
  or or_10 (ALU_AND, ANDI, AND);
  Pull_Resistor pull_resistor_1 (.node(RegDst));
  Pull_Resistor pull_resistor_2 (.node(RegSrc));
  or or_11 (RegSrc[1], RegDst[1], JALR);
  Pull_Resistor pull_resistor_3 (.node(RegWrite));
  Pull_Resistor pull_resistor_4 (.node(ExtOp));
  Pull_Resistor pull_resistor_5 (.node(ALUOp));
  Pull_Resistor pull_resistor_6 (.node(ALUSrc));
  Pull_Resistor pull_resistor_7 (.node(nPC_sel));
  Priority_Encoder #(.select(2)) priority_encoder_3 (
    .in0(Wordwise), .in1(Halfwordwise), .in2(Bytewise), .out(MemOp[1:0]));  // open: in3, gs, en_out, en_in
  Pull_Resistor pull_resistor_8 (.node(MemOp));
  or or_12 (ALU_OR, ORI, OR);
  or or_13 (ALU_SLL, SLL, SLLV);
  or or_14 (ALU_SLT, SLTI, SLT);
  buf or_15 (ALU_SRL, SRL);  // OR_Gate
  or or_16 (_0Ext, ANDI, ORI);
  // OR_Gate or_17 has open pins: out=or_17_out
  or or_18 (SignExt, ADDIU, SW, LW, ALU_EQ, SH, SB, LH, LB);
  or or_19 (Wordwise, LW, SW);
  or or_20 (Halfwordwise, LH, SH);
  or or_21 (Bytewise, LB, SB);
  or or_22 (RegDst[0], ANDI, ORI, ADDIU, HighExt, SLTI, LW, LH, LB);

  // Other names for the same wires on the sheet: ALUSrc_A = ALUSrc[0]; ALUSrc_B = ALUSrc[1]; BEQ = ALU_EQ;
  //   F5 = FUNC[0]; F4 = FUNC[1]; F3 = FUNC[2]; F2 = FUNC[3]; F1 = FUNC[4]; F0 = FUNC[5]; LUI = HighExt;
  //   MemWrite = MemOp[2]; nPC_sel_branch = nPC_sel[0]; nPC_sel_jump_imm = nPC_sel[1]; nPC_sel_jump_reg = nPC_sel[2];
  //   O5 = OP[0]; O4 = OP[1]; O3 = OP[2]; O2 = OP[3]; O1 = OP[4]; O0 = OP[5]; RegDst_t = RegDst[0]; JAL = RegDst[1];
  //   RegSrc_t = RegSrc[0]; SUBU = ALU_SUB
endmodule

module DM (
  input  [2:0] MemOp,
  input  [31:0] RawWD,
  input  [13:0] Addr,
  input  CLK,
  input  RST,
  output [31:0] WD,
  output [31:0] RD
);

  wire [31:0] bit_extender_1_out, bit_extender_2_out, bit_extender_3_out, bit_extender_4_out,
       bit_extender_5_out, bit_extender_6_out, Byte, Half, multiplexer_2_out, multiplexer_3_out, RawRD;

  Multiplexer #(.select(2), .width(32)) multiplexer_1 (
    .in0(RawWD), .in1(Half), .in2(Byte), .out(WD), .sel(MemOp[1:0]));  // open: in3, en
  assign bit_extender_1_out = {{16{RawRD[15]}}, RawRD[15:0]};  // Bit_Extender bit_extender_1
  assign bit_extender_2_out = {{16{RawRD[31]}}, RawRD[31:16]};  // Bit_Extender bit_extender_2
  assign bit_extender_3_out = {{24{RawRD[7]}}, RawRD[7:0]};  // Bit_Extender bit_extender_3
  assign bit_extender_4_out = {{24{RawRD[15]}}, RawRD[15:8]};  // Bit_Extender bit_extender_4
  assign bit_extender_5_out = {{24{RawRD[23]}}, RawRD[23:16]};  // Bit_Extender bit_extender_5
  assign bit_extender_6_out = {{24{RawRD[31]}}, RawRD[31:24]};  // Bit_Extender bit_extender_6
  Multiplexer #(.select(2), .width(32)) multiplexer_2 (
    .in0(bit_extender_1_out), .in2(bit_extender_2_out), .out(multiplexer_2_out), .sel(Addr[1:0]));  // open: in1, in3, en
  Multiplexer #(.select(2), .width(32)) multiplexer_3 (
    .in0(bit_extender_3_out), .in1(bit_extender_4_out), .in2(bit_extender_5_out), .in3(bit_extender_6_out),
    .out(multiplexer_3_out), .sel(Addr[1:0]));  // open: en
  RAM #(.addrWidth(12), .dataWidth(32), .bus("separate")) ram_1 (
    .addr(Addr[13:2]), .din(WD), .data(RawRD), .str(MemOp[2]), .clk(CLK), .clr(RST));  // open: sel, ld
  Multiplexer #(.select(2), .width(32)) multiplexer_4 (
    .in0(RawRD), .in1(multiplexer_2_out), .in2(multiplexer_3_out), .out(RD), .sel(MemOp[1:0]));  // open: in3, en
  Multiplexer #(.select(2), .width(32)) multiplexer_5 (
    .in0({RawRD[31:16], RawWD[15:0]}), .in2({RawWD[15:0], RawRD[15:0]}), .out(Half), .sel(Addr[1:0]));  // open: in1, in3, en
  Multiplexer #(.select(2), .width(32)) multiplexer_6 (
    .in0({RawRD[31:8], RawWD[7:0]}), .in1({RawRD[31:16], RawWD[7:0], RawRD[7:0]}),
    .in2({RawRD[31:24], RawWD[7:0], RawRD[15:0]}), .in3({RawWD[7:0], RawRD[23:0]}), .out(Byte),
    .sel(Addr[1:0]));  // open: en

  // Other names for the same wires on the sheet: pos[1:0] = Addr[1:0]; Addr_t[11:0] = Addr[13:2];
  //   sel[1:0] = MemOp[1:0]; WE = MemOp[2]
endmodule
